# Fritzing sketch Circuit Diagram (saved by Fritzing 0.8.7b)
breadboards: 3

parts:
  Part3 = Arduino Nano (Rev3.0)
  M2 = DC Motor
  M3 = DC Motor
  Part4 = SRF05 Ultrasonic Rangefinder
  U1 = L9110 H-bridge module [part_number="L9110 H-bridge"]
  M4 = fc-51 [package=THT]
  M5 = fc-51 [package=THT]
  U2 = LIPO-1000mAh [package=lipo-1000]
  S1 = Toggle Switch spst [package=THT]
  C1 = Ceramic Capacitor [capacitance="100 nF" package="0603 [SMD, multilayer]"]
  VCC1 = 4 x AAA Battery Mount
  M6 = fc-51 [package=THT]
  M7 = fc-51 [package=THT]
  U3 = LCD-16X2 [package=lcd-16x2]
  U4 = LIPO-1000mAh [package=lipo-1000]
  R1 = Resistor [tolerance=±5% resistance=220 package="0603 [SMD]"]

nets:
  GND: Part3.GND, Part4.GND, U1.GND, M4.pin2, M5.pin2, U2.-, C1.0, VCC1.-, M6.pin2, M7.pin2
  N1: Part3.D2, M7.pin1
  N2: Part3.D3, Part4.Trig
  N3: Part3.D4, Part4.Echo
  N4: Part3.D5, U1.B-IA
  N5: Part3.D6, U1.B-IB
  N6: Part3.D7, M5.pin1
  N7: Part3.D8, M4.pin1
  N8: Part3.D9, U3.E
  N9: Part3.D10, U1.A-IA
  N10: Part3.D11/MOSI, U1.A-IB
  N11: Part3.D12/MISO, U3.RS
  N12: Part3.VIN, S1.COM
  VCC: Part3.5V, Part4.VCC, U1.VCC, U2.+, C1.1, M7.pin3
  N13: Part3.A4, M6.pin1
  N14: Part3.A3, U3.DB6
  N15: Part3.A2, U3.DB5
  N16: Part3.A1, U3.DB4
  N17: Part3.A0, U3.DB3
  N18: Part3.3V3, M4.pin3, M5.pin3, M6.pin3
  N19: M2.pin_1, U1.MOTOR_B-B
  N20: M2.pin_2, U1.MOTOR_B-A
  N21: M3.pin_1, U1.MOTOR_A-B
  N22: M3.pin_2, U1.MOTOR_A-A
  N23: S1.L1, VCC1.+
  N24: U3.VSS, U3.R_W, U3.K, U4.-
  N25: U3.VDD, U4.+, R1.Pin_0
  N26: U3.A, R1.Pin_1

custom parts:
  Toggle Switch spst: Toggle Switch single pole single throw
